# Fritzing sketch esquema (saved by Fritzing 0.9.3b)
breadboards: 1

parts:
  Controlador = Arduino Mega 2560 (Rev3)
  Servo_1_(SG90) = Basic Servo
  Servo_2_(SG90) = Basic Servo
  R1 = Resistor [tolerance=±5% resistance=10k package="0603 [SMD]"]
  LDR4 = Photocell (LDR) [package=THT]
  C1_(3300uf_6_3v) = Electrolytic Capacitor
  R2 = Resistor [tolerance=±5% resistance=10k package="0603 [SMD]"]
  LDR3 = Photocell (LDR) [package=THT]
  R3 = Resistor [tolerance=±5% resistance=10k package="0603 [SMD]"]
  LDR2 = Photocell (LDR) [package=THT]
  R4 = Resistor [tolerance=±5% resistance=10k package="0603 [SMD]"]
  LDR1 = Photocell (LDR) [package=THT]
  D1 = SOLAR-IXYS [package=solarbit-12x1]
  part = INA219 High Side DC Current Sensor Breakout [part_number=904]
  VCC1 = 4 x AAA Battery Mount

nets:
  N1: Controlador.A0, R1.Pin_1, LDR4.pin_0
  N2: Controlador.A1, R2.Pin_1, LDR3.pin_0
  N3: Controlador.A2, R3.Pin_1, LDR2.pin_0
  N4: Controlador.A3, R4.Pin_1, LDR1.pin_0
  N5: Controlador.D21/SCL, part.SCL
  N6: Controlador.D20/SDA, part.SDA
  N7: Controlador.D11_PWM, Servo_2_(SG90).pulse
  N8: Controlador.D9_PWM, Servo_1_(SG90).pulse
  VCC: Controlador.5V, Servo_1_(SG90).vcc, Servo_2_(SG90).vcc, LDR4.pin_1, C1_(3300uf_6_3v).+, LDR3.pin_1, LDR2.pin_1, LDR1.pin_1, part.VCC
  GND: Controlador.GND, Servo_1_(SG90).gnd, Servo_2_(SG90).gnd, R1.Pin_0, C1_(3300uf_6_3v).Capacitor_3300uf, R2.Pin_0, R3.Pin_0, R4.Pin_0, D1.C, part.GND, VCC1.-
  N9: D1.A, part.VIN+
  N10: part.VIN-, VCC1.+

custom parts:
  Electrolytic Capacitor: 1000µF electrolytic capacitor
  INA219 High Side DC Current Sensor Breakout: This breakout board will solve all your power-monitoring problems. Instead of struggling with two multimeters, you can just use the handy INA219B chip on this breakout to both measure both the high side voltage and DC current draw over I2C with 1% precision. Most current-measuring devices such as our current panel meter are only good for low side measuring. That means that unless you want to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
